# Fritzing sketch scheme (saved by Fritzing 1.0.5)
circuit board: 8.46667cm x 5.64444cm

parts:
  Part1 = ws2812b [package="smd 2812b"]
  M1 = Osoyoo SX1278-ra-02
  WeMos_D1_Mini1 = WeMos D1 Mini
  WeMos_D1_Mini2 = WeMos D1 Mini
  M2 = Osoyoo SX1278-ra-02
  KF-1 = KF-301 Relay [package=THT]
  Part2 = ws2812b [package="smd 2812b"]
  HDO = Taiway 100-SP-X-T1 SPDT Miniature Toggle Switch [part_number=100-SP-X-T1-0-0-B1-M1 package=THT]

nets:
  VDD: Part1.VDD, WeMos_D1_Mini1.5V
  VSS: Part1.VSS, M1.GND, WeMos_D1_Mini1.G, HDO.COM
  N1: Part1.DIN, WeMos_D1_Mini1.D3
  3.3V: M1.3.3V, WeMos_D1_Mini1.3V3
  N2: M1.RST, WeMos_D1_Mini1.D0
  N3: M1.DIO0, WeMos_D1_Mini1.D1
  N4: M1.SCK, WeMos_D1_Mini1.D5
  N5: M1.MISO, WeMos_D1_Mini1.D6
  N6: M1.MOSI, WeMos_D1_Mini1.D7
  N7: M1.NSS, WeMos_D1_Mini1.D8
  N8: WeMos_D1_Mini1.D2, HDO.L1
  3V3: WeMos_D1_Mini2.3V3, M2.3.3V
  5V: WeMos_D1_Mini2.5V, KF-1.power, Part2.VDD
  N9: WeMos_D1_Mini2.D0, M2.RST
  N10: WeMos_D1_Mini2.D1, M2.DIO0
  N11: WeMos_D1_Mini2.D2, KF-1.signal
  N12: WeMos_D1_Mini2.D3, Part2.DIN
  N13: WeMos_D1_Mini2.D5, M2.SCK
  N14: WeMos_D1_Mini2.D6, M2.MISO
  N15: WeMos_D1_Mini2.D7, M2.MOSI
  N16: WeMos_D1_Mini2.D8, M2.NSS
  N17: WeMos_D1_Mini2.G, M2.GND, KF-1.ground

notes:
  TX
  RX
  HDO switch

custom parts:
  Osoyoo SX1278-ra-02: Osoyoo Long Distance wireless transceiver Uart LoRa Module.
  KF-301 Relay: KF-301
